// Logisim project cpu.circ as structural Verilog: 1 circuit, main circuit main
// EN
module main (
  input  EN,
  output [15:0] out_2
);

  wire and_1_out, and_2_out, and_3_out, and_4_out, and_5_out, and_6_out, and_7_out, and_8_out, and_9_out,
       and_10_out, and_11_out, and_12_out, and_13_out, and_14_out, and_15_out, and_16_out, and_17_out,
       and_18_out, and_19_out, and_20_out, and_21_out, and_22_out, and_23_out, and_24_out, and_25_out,
       and_26_out, and_27_out, and_28_out, and_29_out, and_30_out, and_31_out, and_32_out, and_33_out,
       and_34_out, and_35_out, and_36_out, and_37_out, and_38_out, and_39_out, and_40_out, and_41_out,
       and_42_out, and_43_out, and_44_out, and_45_out, and_46_out, and_47_out, and_48_out, and_49_out,
       and_50_out, and_51_out, and_52_out, and_53_out, CLK, comparator_1_eq, D0, D1, D2, D3, D4, D5, D6, D7,
       D8, D9, D10, D11, D12, D13, D14, D15, D16, D17, D18, decoder_7_out0, decoder_7_out1, EN_IR, L_H,
       M_CLR, M_LD, M_SEL, M_STR, MUXCSEL, not_1_out, not_2_out, not_3_out, not_4_out, not_5_out, not_6_out,
       not_7_out, not_8_out, not_9_out, not_10_out, not_11_out, not_12_out, not_13_out, not_14_out,
       not_15_out, not_16_out, or_1_out, or_2_out, or_3_out, or_6_out, or_7_out, or_8_out, or_9_out,
       or_10_out, or_11_out, or_12_out, or_13_out, or_14_out, or_15_out, or_16_out, or_17_out, or_18_out,
       or_20_out, or_21_out, or_22_out, or_23_out, SC, T0, T1, T2, T3, T4, T5, T6, T7, WithAddress;
  wire [1:0] des_4bit, FUNSEL_ARF, FUNSEL_IR, FUNSEL_RF, multiplexer_1_out, MUXASEL, MUXBSEL, N_A_RF,
       OUTASEL, OUTBSEL, OUTCSEL, OUTDSEL, s1_01c, s2_01c, subtractor_1_out;
  wire [2:0] counter_1_q, des_3bit, N_A_ARF, REGSEL_ARF, s1_3bit;
  wire [3:0] FLAG, FUNSEL_ALU, OPERATION, REGSEL, REGSEL_RF, s2_4bit;
  wire [7:0] IR_HIGH;

  and and_1 (and_1_out, T2, WithAddress, out_2[8]);
  and and_2 (and_2_out, T3, D0);
  Multiplexer #(.width(2)) multiplexer_1 (.in0(2'b11), .in1(2'b10), .out(multiplexer_1_out), .sel(D8), .en(EN));
  assign MUXBSEL = and_1_out ? 2'b01 : 2'bz;  // Controlled_Buffer controlled_buffer_1
  assign FUNSEL_ARF = and_1_out ? 2'b01 : 2'bz;  // Controlled_Buffer controlled_buffer_2
  assign REGSEL_ARF = and_1_out ? 3'b010 : 3'bz;  // Controlled_Buffer controlled_buffer_3
  assign MUXASEL = and_2_out ? {1'b0, out_2[8]} : 2'bz;  // Controlled_Buffer controlled_buffer_4
  assign REGSEL_RF = and_2_out ? REGSEL : 4'bz;  // Controlled_Buffer controlled_buffer_5
  assign FUNSEL_RF = and_2_out ? 2'b01 : 2'bz;  // Controlled_Buffer controlled_buffer_6
  Controlled_Buffer #(.width(2)) controlled_buffer_7 (.out(FUNSEL_RF), .en(and_2_out));  // open: in
  assign OUTDSEL = and_2_out ? 2'b01 : 2'bz;  // Controlled_Buffer controlled_buffer_8
  assign M_STR = and_2_out ? 1'b0 : 1'bz;  // Controlled_Buffer controlled_buffer_9
  assign M_SEL = and_2_out ? 1'b1 : 1'bz;  // Controlled_Buffer controlled_buffer_10
  assign M_LD = and_2_out ? 1'b1 : 1'bz;  // Controlled_Buffer controlled_buffer_11
  assign M_CLR = and_2_out ? 1'b0 : 1'bz;  // Controlled_Buffer controlled_buffer_12
  or or_1 (or_1_out, D7, D8);
  and and_3 (and_3_out, or_1_out, out_2[7], T2);
  assign FUNSEL_ARF = and_3_out ? multiplexer_1_out : 2'bz;  // Controlled_Buffer controlled_buffer_13
  assign REGSEL_ARF = and_3_out ? N_A_ARF : 3'bz;  // Controlled_Buffer controlled_buffer_14
  Decoder #(.select(2)) decoder_1 (
    .out0(N_A_RF[0]), .out1(N_A_RF[1]), .out2(N_A_ARF[1]), .out3(N_A_ARF[2]), .sel(out_2[9:8]), .en(EN));
  Decoder #(.select(2)) decoder_2 (
    .out0(REGSEL[0]), .out1(REGSEL[1]), .out2(REGSEL[2]), .out3(REGSEL[3]), .sel(out_2[10:9]), .en(EN));
  and and_4 (and_4_out, D2, T2);
  not not_1 (not_1_out, out_2[7]);
  or or_2 (or_2_out, D11, D12, D13);
  and and_5 (and_5_out, or_2_out, T2);
  or or_3 (or_3_out, and_4_out, and_5_out, and_8_out);
  not not_2 (not_2_out, out_2[7]);
  and and_6 (and_6_out, out_2[10], and_9_out);
  assign MUXBSEL = and_6_out ? 2'b11 : 2'bz;  // Controlled_Buffer controlled_buffer_15
  assign FUNSEL_ARF = and_6_out ? 2'b01 : 2'bz;  // Controlled_Buffer controlled_buffer_16
  assign REGSEL_ARF = and_6_out ? N_A_ARF : 3'bz;  // Controlled_Buffer controlled_buffer_17
  or or_4 (N_A_ARF[0], N_A_RF[0], N_A_RF[1]);
  project2_2_main main_1 (
    .EN(EN), .MuxCSel(MUXCSEL), .OutASel(OUTASEL), .OutBSel(OUTBSEL), .FunSel_2(FUNSEL_RF),
    .RegSel(REGSEL_RF), .MuxASel(MUXASEL), .MuxBSel(MUXBSEL), .OutCSel(OUTCSEL), .OutDSel(OUTDSEL),
    .FunSel_3(FUNSEL_ARF), .RegSel_2(REGSEL_ARF), .L___H_prime(L_H), .FUNSEL_4(FUNSEL_IR), .CLK(CLK),
    .IR(out_2), .FlagRegister(FLAG), .IR__8_15(IR_HIGH), .FunSel(FUNSEL_ALU), .in_11(M_STR), .in_12(M_SEL),
    .in_13(M_LD), .in_14(M_CLR), .EN_IR(EN_IR));
  or or_5 (WithAddress, D0, D1);
  and and_7 (and_7_out, not_1_out, or_1_out, T2);
  assign FUNSEL_RF = and_7_out ? multiplexer_1_out : 2'bz;  // Controlled_Buffer controlled_buffer_18
  assign REGSEL_RF = and_7_out ? {N_A_ARF[2:1], N_A_RF} : 4'bz;  // Controlled_Buffer controlled_buffer_19
  or or_6 (or_6_out, D7, D8);
  and and_8 (and_8_out, or_6_out, T3);
  and and_9 (and_9_out, not_2_out, or_3_out);
  assign OUTASEL = and_9_out ? out_2[6:5] : 2'bz;  // Controlled_Buffer controlled_buffer_20
  assign MUXCSEL = and_9_out ? 1'b1 : 1'bz;  // Controlled_Buffer controlled_buffer_21
  assign FUNSEL_ALU = and_9_out ? OPERATION : 4'bz;  // Controlled_Buffer controlled_buffer_22
  not not_3 (not_3_out, out_2[10]);
  and and_10 (and_10_out, D1, T3);
  assign OUTBSEL = and_10_out ? out_2[10:9] : 2'bz;  // Controlled_Buffer controlled_buffer_23
  assign FUNSEL_ALU = and_10_out ? 4'b0001 : 4'bz;  // Controlled_Buffer controlled_buffer_24
  assign M_STR = and_10_out ? 1'b1 : 1'bz;  // Controlled_Buffer controlled_buffer_25
  assign M_SEL = and_10_out ? 1'b1 : 1'bz;  // Controlled_Buffer controlled_buffer_26
  assign M_LD = and_10_out ? 1'b0 : 1'bz;  // Controlled_Buffer controlled_buffer_27
  assign M_CLR = and_10_out ? 1'b0 : 1'bz;  // Controlled_Buffer controlled_buffer_28
  assign OUTDSEL = and_10_out ? 2'b01 : 2'bz;  // Controlled_Buffer controlled_buffer_29
  or or_7 (or_7_out, D2, D7, D8);
  assign OPERATION = or_7_out ? 4'b0000 : 4'bz;  // Controlled_Buffer controlled_buffer_30
  not not_4 (not_4_out, not_2_out);
  and and_11 (and_11_out, and_9_out, not_3_out);
  assign MUXASEL = and_11_out ? 2'b11 : 2'bz;  // Controlled_Buffer controlled_buffer_31
  assign FUNSEL_RF = and_11_out ? 2'b01 : 2'bz;  // Controlled_Buffer controlled_buffer_32
  assign REGSEL_RF = and_11_out ? {N_A_ARF[2:1], N_A_RF} : 4'bz;  // Controlled_Buffer controlled_buffer_33
  Subtractor #(.width(2)) subtractor_1 (.a(out_2[6:5]), .b(2'b01), .out(subtractor_1_out));  // open: bin, bout
  Decoder #(.select(5)) decoder_3 (
    .out0(D0), .out1(D1), .out2(D2), .out3(D3), .out4(D4), .out5(D5), .out6(D6), .out7(D7), .out8(D8),
    .out9(D9), .out10(D10), .out11(D11), .out12(D12), .out13(D13), .out14(D14), .out15(D15), .out16(D16),
    .out17(D17), .out18(D18), .sel(out_2[15:11]), .en(EN));  // open: out19, out20, out21, out22, out23, out24, out25, out26, out27, out28, out29, out30, out31
  assign OPERATION = D11 ? 4'b0010 : 4'bz;  // Controlled_Buffer controlled_buffer_34
  and and_12 (and_12_out, not_4_out, or_3_out);
  and and_13 (and_13_out, and_12_out, not_3_out);
  and and_14 (and_14_out, and_12_out, not_5_out);
  not not_5 (not_5_out, not_3_out);
  assign OUTDSEL = T0 ? 2'b00 : 2'bz;  // Controlled_Buffer controlled_buffer_35
  assign M_SEL = T0 ? 1'b1 : 1'bz;  // Controlled_Buffer controlled_buffer_36
  assign M_LD = T0 ? 1'b1 : 1'bz;  // Controlled_Buffer controlled_buffer_37
  assign M_STR = T0 ? 1'b0 : 1'bz;  // Controlled_Buffer controlled_buffer_38
  assign M_CLR = T0 ? 1'b0 : 1'bz;  // Controlled_Buffer controlled_buffer_39
  assign L_H = T0 ? 1'b1 : 1'bz;  // Controlled_Buffer controlled_buffer_40
  assign FUNSEL_IR = T0 ? 2'b11 : 2'bz;  // Controlled_Buffer controlled_buffer_41
  assign REGSEL_ARF = T0 ? 3'b001 : 3'bz;  // Controlled_Buffer controlled_buffer_42
  assign FUNSEL_ARF = T0 ? 2'b10 : 2'bz;  // Controlled_Buffer controlled_buffer_43
  and and_15 (and_15_out, T2, D3);
  assign OUTBSEL = and_15_out ? out_2[9:8] : 2'bz;  // Controlled_Buffer controlled_buffer_44
  assign FUNSEL_ALU = and_15_out ? 4'b0001 : 4'bz;  // Controlled_Buffer controlled_buffer_45
  assign OUTDSEL = and_15_out ? 2'b10 : 2'bz;  // Controlled_Buffer controlled_buffer_46
  assign M_SEL = and_15_out ? 1'b1 : 1'bz;  // Controlled_Buffer controlled_buffer_47
  assign M_LD = and_15_out ? 1'b0 : 1'bz;  // Controlled_Buffer controlled_buffer_48
  assign M_STR = and_15_out ? 1'b1 : 1'bz;  // Controlled_Buffer controlled_buffer_49
  assign M_CLR = and_15_out ? 1'b0 : 1'bz;  // Controlled_Buffer controlled_buffer_50
  and and_16 (and_16_out, T3, D3);
  assign FUNSEL_ARF = and_16_out ? 2'b11 : 2'bz;  // Controlled_Buffer controlled_buffer_51
  assign REGSEL_ARF = and_16_out ? 3'b100 : 3'bz;  // Controlled_Buffer controlled_buffer_52
  assign OPERATION = D13 ? 4'b1011 : 4'bz;  // Controlled_Buffer controlled_buffer_53
  assign OPERATION = D12 ? 4'b1010 : 4'bz;  // Controlled_Buffer controlled_buffer_54
  and and_17 (and_17_out, and_13_out, D2);
  assign OUTCSEL = and_17_out ? subtractor_1_out : 2'bz;  // Controlled_Buffer controlled_buffer_55
  assign MUXASEL = and_17_out ? 2'b10 : 2'bz;  // Controlled_Buffer controlled_buffer_56
  assign FUNSEL_RF = and_17_out ? 2'b01 : 2'bz;  // Controlled_Buffer controlled_buffer_57
  assign REGSEL_RF = and_17_out ? {N_A_ARF[2:1], N_A_RF} : 4'bz;  // Controlled_Buffer controlled_buffer_58
  assign OUTCSEL = and_14_out ? subtractor_1_out : 2'bz;  // Controlled_Buffer controlled_buffer_59
  assign MUXASEL = and_14_out ? 2'b10 : 2'bz;  // Controlled_Buffer controlled_buffer_60
  assign MUXCSEL = and_14_out ? 1'b0 : 1'bz;  // Controlled_Buffer controlled_buffer_61
  assign FUNSEL_ALU = and_14_out ? OPERATION : 4'bz;  // Controlled_Buffer controlled_buffer_62
  assign MUXBSEL = and_14_out ? 2'b11 : 2'bz;  // Controlled_Buffer controlled_buffer_63
  assign FUNSEL_ARF = and_14_out ? 2'b01 : 2'bz;  // Controlled_Buffer controlled_buffer_64
  assign REGSEL_ARF = and_14_out ? N_A_ARF : 3'bz;  // Controlled_Buffer controlled_buffer_65
  and and_18 (and_18_out, not_3_out, not_4_out);
  Clock clock_1 (.out(CLK));
  assign OUTDSEL = T1 ? 2'b00 : 2'bz;  // Controlled_Buffer controlled_buffer_66
  assign M_SEL = T1 ? 1'b1 : 1'bz;  // Controlled_Buffer controlled_buffer_67
  assign M_LD = T1 ? 1'b1 : 1'bz;  // Controlled_Buffer controlled_buffer_68
  assign M_STR = T1 ? 1'b0 : 1'bz;  // Controlled_Buffer controlled_buffer_69
  assign M_CLR = T1 ? 1'b0 : 1'bz;  // Controlled_Buffer controlled_buffer_70
  assign L_H = T1 ? 1'b0 : 1'bz;  // Controlled_Buffer controlled_buffer_71
  assign FUNSEL_IR = T1 ? 2'b11 : 2'bz;  // Controlled_Buffer controlled_buffer_72
  assign REGSEL_ARF = T1 ? 3'b001 : 3'bz;  // Controlled_Buffer controlled_buffer_73
  assign FUNSEL_ARF = T1 ? 2'b10 : 2'bz;  // Controlled_Buffer controlled_buffer_74
  or or_8 (or_8_out, D7, D11, D12, D13, D8);
  and and_19 (and_19_out, and_18_out, or_8_out);
  assign OUTCSEL = and_19_out ? subtractor_1_out : 2'bz;  // Controlled_Buffer controlled_buffer_75
  assign MUXASEL = and_19_out ? 2'b10 : 2'bz;  // Controlled_Buffer controlled_buffer_76
  assign MUXCSEL = and_19_out ? 1'b0 : 1'bz;  // Controlled_Buffer controlled_buffer_77
  assign FUNSEL_ALU = and_19_out ? OPERATION : 4'bz;  // Controlled_Buffer controlled_buffer_78
  and and_20 (and_20_out, T2, D4);
  assign FUNSEL_ARF = and_20_out ? 2'b10 : 2'bz;  // Controlled_Buffer controlled_buffer_79
  assign REGSEL_ARF = and_20_out ? 3'b100 : 3'bz;  // Controlled_Buffer controlled_buffer_80
  and and_21 (and_21_out, T3, D4);
  assign OUTDSEL = and_21_out ? 2'b10 : 2'bz;  // Controlled_Buffer controlled_buffer_81
  assign M_SEL = and_21_out ? 1'b1 : 1'bz;  // Controlled_Buffer controlled_buffer_82
  assign M_LD = and_21_out ? 1'b1 : 1'bz;  // Controlled_Buffer controlled_buffer_83
  assign M_STR = and_21_out ? 1'b0 : 1'bz;  // Controlled_Buffer controlled_buffer_84
  assign M_CLR = and_21_out ? 1'b0 : 1'bz;  // Controlled_Buffer controlled_buffer_85
  assign MUXASEL = and_21_out ? 2'b01 : 2'bz;  // Controlled_Buffer controlled_buffer_86
  assign FUNSEL_RF = and_21_out ? 2'b01 : 2'bz;  // Controlled_Buffer controlled_buffer_87
  assign REGSEL_RF = and_21_out ? {des_3bit[2:1], des_4bit} : 4'bz;  // Controlled_Buffer controlled_buffer_88
  Counter #(.width(3), .max('h7)) counter_1 (.Q(counter_1_q), .clk(CLK), .clr(SC));  // open: load, D, count, carry
  Decoder #(.select(3)) decoder_4 (
    .out0(T0), .out1(T1), .out2(T2), .out3(T3), .out4(T4), .out5(T5), .out6(T6), .out7(T7),
    .sel(counter_1_q), .en(EN));
  or or_9 (or_9_out, T0, T1);
  assign EN_IR = or_9_out ? 1'b1 : 1'bz;  // Controlled_Buffer controlled_buffer_89
  or or_10 (or_10_out, D3, D4, D5, D6, D9, D10, D14, D15, D16);
  or or_11 (or_11_out, out_2[7], out_2[4]);
  and and_22 (and_22_out, or_10_out, T3);
  and and_23 (and_23_out, or_11_out, out_2[7], out_2[10]);
  Comparator #(.width(3)) comparator_1 (.a(out_2[7:5]), .b(out_2[10:8]), .eq(comparator_1_eq));  // open: gt, lt
  or or_12 (or_12_out, D7, D8);
  or or_13 (or_13_out, D0, D1, D18, D11, D12, D13);
  and and_24 (and_24_out, or_13_out, T4);
  and and_25 (and_25_out, and_23_out, T3, or_17_out);
  assign OUTCSEL = and_25_out ? s2_01c : 2'bz;  // Controlled_Buffer controlled_buffer_90
  assign MUXASEL = and_25_out ? 2'b10 : 2'bz;  // Controlled_Buffer controlled_buffer_91
  assign MUXCSEL = and_25_out ? 1'b0 : 1'bz;  // Controlled_Buffer controlled_buffer_92
  assign OUTBSEL = and_25_out ? out_2[3:2] : 2'bz;  // Controlled_Buffer controlled_buffer_93
  assign FUNSEL_ALU = and_25_out ? OPERATION : 4'bz;  // Controlled_Buffer controlled_buffer_94
  assign MUXBSEL = and_25_out ? 2'b11 : 2'bz;  // Controlled_Buffer controlled_buffer_95
  assign REGSEL_ARF = and_25_out ? des_3bit : 3'bz;  // Controlled_Buffer controlled_buffer_96
  assign FUNSEL_ARF = and_25_out ? 2'b01 : 2'bz;  // Controlled_Buffer controlled_buffer_97
  not not_6 (not_6_out, comparator_1_eq);
  and and_26 (and_26_out, or_12_out, not_6_out, T4);
  or or_14 (or_14_out, D11, D12, D13);
  and and_27 (and_27_out, or_14_out, T3);
  assign MUXASEL = and_27_out ? 2'b10 : 2'bz;  // Controlled_Buffer controlled_buffer_98
  assign FUNSEL_RF = and_27_out ? 2'b01 : 2'bz;  // Controlled_Buffer controlled_buffer_99
  assign REGSEL_RF = and_27_out ? {N_A_ARF[2:1], N_A_RF} : 4'bz;  // Controlled_Buffer controlled_buffer_100
  or or_15 (or_15_out, D7, D8);
  or or_16 (or_16_out, and_22_out, and_24_out, and_28_out, and_31_out);
  assign SC = or_16_out ? 1'b1 : 1'bz;  // Controlled_Buffer controlled_buffer_101
  or or_17 (or_17_out, D5, D6, D9, D10);
  not not_7 (not_7_out, out_2[7]);
  and and_28 (and_28_out, or_15_out, T5);
  or or_18 (or_18_out, out_2[7], out_2[4]);
  not not_8 (not_8_out, out_2[10]);
  and and_29 (and_29_out, and_26_out, out_2[7]);
  assign FUNSEL_ARF = and_29_out ? {1'b1, D8} : 2'bz;  // Controlled_Buffer controlled_buffer_102
  assign REGSEL_ARF = and_29_out ? N_A_ARF : 3'bz;  // Controlled_Buffer controlled_buffer_103
  and and_30 (and_30_out, and_26_out, not_7_out);
  assign FUNSEL_RF = and_30_out ? {1'b1, D8} : 2'bz;  // Controlled_Buffer controlled_buffer_104
  assign REGSEL_RF = and_30_out ? {N_A_ARF[2:1], N_A_RF} : 4'bz;  // Controlled_Buffer controlled_buffer_105
  and and_31 (and_31_out, D17, T6);
  and and_32 (and_32_out, or_18_out, not_8_out);
  and and_33 (and_33_out, and_32_out, T3, or_17_out);
  assign OUTASEL = and_33_out ? out_2[9:8] : 2'bz;  // Controlled_Buffer controlled_buffer_106
  assign OUTBSEL = and_33_out ? out_2[6:5] : 2'bz;  // Controlled_Buffer controlled_buffer_107
  assign MUXCSEL = and_33_out ? 1'b1 : 1'bz;  // Controlled_Buffer controlled_buffer_108
  assign FUNSEL_ALU = and_33_out ? OPERATION : 4'bz;  // Controlled_Buffer controlled_buffer_109
  assign MUXASEL = and_33_out ? 2'b11 : 2'bz;  // Controlled_Buffer controlled_buffer_110
  assign REGSEL_RF = and_33_out ? {des_3bit[2:1], des_4bit} : 4'bz;  // Controlled_Buffer controlled_buffer_111
  assign FUNSEL_RF = and_33_out ? 2'b01 : 2'bz;  // Controlled_Buffer controlled_buffer_112
  Decoder #(.select(2)) decoder_5 (
    .out0(des_4bit[0]), .out1(des_4bit[1]), .out2(des_3bit[1]), .out3(des_3bit[2]), .sel(out_2[9:8]), .en(EN));
  or or_19 (des_3bit[0], des_4bit[0], des_4bit[1]);
  and and_34 (and_34_out, D14, T2);
  Decoder #(.select(2)) decoder_6 (
    .out0(s2_4bit[0]), .out1(s2_4bit[1]), .out2(s2_4bit[2]), .out3(s2_4bit[3]), .sel(out_2[3:2]), .en(EN));
  and and_35 (and_35_out, T2, or_22_out);
  and and_36 (and_36_out, and_35_out, or_20_out);
  or or_20 (or_20_out, out_2[7], out_2[4]);
  and and_37 (and_37_out, out_2[10], and_36_out);
  and and_38 (and_38_out, out_2[7], and_37_out);
  and and_39 (and_39_out, FLAG[3], D15, T2);
  or or_21 (or_21_out, and_34_out, and_39_out, and_41_out);
  or or_22 (or_22_out, D5, D6, D9, D10);
  assign OUTBSEL = and_38_out ? out_2[3:2] : 2'bz;  // Controlled_Buffer controlled_buffer_113
  assign FUNSEL_ALU = and_38_out ? 4'b0001 : 4'bz;  // Controlled_Buffer controlled_buffer_114
  assign MUXBSEL = and_38_out ? 2'b11 : 2'bz;  // Controlled_Buffer controlled_buffer_115
  assign OUTCSEL = and_38_out ? s1_01c : 2'bz;  // Controlled_Buffer controlled_buffer_116
  assign MUXASEL = and_38_out ? 2'b10 : 2'bz;  // Controlled_Buffer controlled_buffer_117
  assign REGSEL_RF = and_38_out ? s2_4bit : 4'bz;  // Controlled_Buffer controlled_buffer_118
  assign FUNSEL_RF = and_38_out ? 2'b01 : 2'bz;  // Controlled_Buffer controlled_buffer_119
  assign REGSEL_ARF = and_38_out ? s1_3bit : 3'bz;  // Controlled_Buffer controlled_buffer_120
  assign FUNSEL_ARF = and_38_out ? 2'b01 : 2'bz;  // Controlled_Buffer controlled_buffer_121
  not not_9 (not_9_out, out_2[8]);
  and and_40 (and_40_out, or_21_out, not_9_out);
  assign MUXBSEL = and_40_out ? 2'b01 : 2'bz;  // Controlled_Buffer controlled_buffer_122
  assign REGSEL_ARF = and_40_out ? 3'b001 : 3'bz;  // Controlled_Buffer controlled_buffer_123
  assign FUNSEL_ARF = and_40_out ? 2'b01 : 2'bz;  // Controlled_Buffer controlled_buffer_124
  or or_23 (or_23_out, D14, D16);
  assign M_SEL = or_23_out ? 1'b0 : 1'bz;  // Controlled_Buffer controlled_buffer_125
  assign M_LD = or_23_out ? 1'b1 : 1'bz;  // Controlled_Buffer controlled_buffer_126
  assign M_STR = or_23_out ? 1'b0 : 1'bz;  // Controlled_Buffer controlled_buffer_127
  assign M_CLR = or_23_out ? 1'b0 : 1'bz;  // Controlled_Buffer controlled_buffer_128
  not not_10 (not_10_out, FLAG[3]);
  and and_41 (and_41_out, not_10_out, D16, T2);
  Decoder #(.select(2)) decoder_7 (
    .out0(decoder_7_out0), .out1(decoder_7_out1), .out2(s1_3bit[1]), .out3(s1_3bit[2]), .sel(out_2[6:5]),
    .en(EN));
  and and_42 (and_42_out, and_37_out, out_2[4]);
  assign OUTCSEL = and_42_out ? s2_01c : 2'bz;  // Controlled_Buffer controlled_buffer_129
  assign MUXASEL = and_42_out ? 2'b10 : 2'bz;  // Controlled_Buffer controlled_buffer_130
  assign MUXCSEL = and_42_out ? 1'b0 : 1'bz;  // Controlled_Buffer controlled_buffer_131
  assign OUTBSEL = and_42_out ? out_2[6:5] : 2'bz;  // Controlled_Buffer controlled_buffer_132
  assign FUNSEL_ALU = and_42_out ? OPERATION : 4'bz;  // Controlled_Buffer controlled_buffer_133
  assign MUXBSEL = and_42_out ? 2'b11 : 2'bz;  // Controlled_Buffer controlled_buffer_134
  assign REGSEL_ARF = and_42_out ? des_3bit : 3'bz;  // Controlled_Buffer controlled_buffer_135
  assign FUNSEL_ARF = and_42_out ? 2'b01 : 2'bz;  // Controlled_Buffer controlled_buffer_136
  or or_24 (s1_3bit[0], decoder_7_out0, decoder_7_out1);
  assign OPERATION = D5 ? 4'b0100 : 4'bz;  // Controlled_Buffer controlled_buffer_137
  assign OPERATION = D6 ? 4'b0110 : 4'bz;  // Controlled_Buffer controlled_buffer_138
  and and_43 (and_43_out, out_2[7], and_47_out);
  not not_11 (not_11_out, out_2[8]);
  and and_44 (and_44_out, T3, D17, not_11_out);
  assign OUTDSEL = and_44_out ? 2'b10 : 2'bz;  // Controlled_Buffer controlled_buffer_139
  assign OUTCSEL = and_44_out ? 2'b00 : 2'bz;  // Controlled_Buffer controlled_buffer_140
  assign MUXASEL = and_44_out ? 2'b10 : 2'bz;  // Controlled_Buffer controlled_buffer_141
  assign MUXCSEL = and_44_out ? 1'b0 : 1'bz;  // Controlled_Buffer controlled_buffer_142
  assign FUNSEL_ALU = and_44_out ? 4'b0000 : 4'bz;  // Controlled_Buffer controlled_buffer_143
  not not_12 (not_12_out, out_2[8]);
  and and_45 (and_45_out, T4, D17, not_12_out);
  assign M_SEL = and_45_out ? 1'b1 : 1'bz;  // Controlled_Buffer controlled_buffer_144
  assign M_STR = and_45_out ? 1'b1 : 1'bz;  // Controlled_Buffer controlled_buffer_145
  assign REGSEL_ARF = and_45_out ? 3'b100 : 3'bz;  // Controlled_Buffer controlled_buffer_146
  assign FUNSEL_ARF = and_45_out ? 2'b11 : 2'bz;  // Controlled_Buffer controlled_buffer_147
  not not_13 (not_13_out, out_2[8]);
  and and_46 (and_46_out, T5, D17, not_13_out);
  assign MUXBSEL = and_46_out ? 2'b01 : 2'bz;  // Controlled_Buffer controlled_buffer_148
  assign REGSEL_ARF = and_46_out ? 3'b001 : 3'bz;  // Controlled_Buffer controlled_buffer_149
  assign FUNSEL_ARF = and_46_out ? 2'b01 : 2'bz;  // Controlled_Buffer controlled_buffer_150
  not not_14 (not_14_out, or_20_out);
  not not_15 (not_15_out, out_2[10]);
  and and_47 (and_47_out, not_15_out, and_36_out);
  assign OUTCSEL = and_43_out ? s1_01c : 2'bz;  // Controlled_Buffer controlled_buffer_151
  assign MUXASEL = and_43_out ? 2'b10 : 2'bz;  // Controlled_Buffer controlled_buffer_152
  assign REGSEL_RF = and_43_out ? {des_3bit[2:1], des_4bit} : 4'bz;  // Controlled_Buffer controlled_buffer_153
  assign FUNSEL_RF = and_43_out ? 2'b01 : 2'bz;  // Controlled_Buffer controlled_buffer_154
  assign OPERATION = D9 ? 4'b0111 : 4'bz;  // Controlled_Buffer controlled_buffer_155
  assign OPERATION = D10 ? 4'b1000 : 4'bz;  // Controlled_Buffer controlled_buffer_156
  and and_48 (and_48_out, T2, D18);
  and and_49 (and_49_out, T3, D18);
  and and_50 (and_50_out, and_47_out, out_2[4]);
  assign OUTCSEL = and_50_out ? s2_01c : 2'bz;  // Controlled_Buffer controlled_buffer_157
  assign MUXASEL = and_50_out ? 2'b10 : 2'bz;  // Controlled_Buffer controlled_buffer_158
  assign REGSEL_RF = and_50_out ? {des_3bit[2:1], des_4bit} : 4'bz;  // Controlled_Buffer controlled_buffer_159
  assign FUNSEL_RF = and_50_out ? 2'b01 : 2'bz;  // Controlled_Buffer controlled_buffer_160
  assign REGSEL_ARF = and_48_out ? 3'b100 : 3'bz;  // Controlled_Buffer controlled_buffer_161
  assign FUNSEL_ARF = and_48_out ? 2'b10 : 2'bz;  // Controlled_Buffer controlled_buffer_162
  assign OUTDSEL = and_49_out ? 2'b10 : 2'bz;  // Controlled_Buffer controlled_buffer_163
  assign M_LD = and_49_out ? 1'b1 : 1'bz;  // Controlled_Buffer controlled_buffer_164
  assign M_SEL = and_49_out ? 1'b1 : 1'bz;  // Controlled_Buffer controlled_buffer_165
  assign MUXBSEL = and_49_out ? 2'b10 : 2'bz;  // Controlled_Buffer controlled_buffer_166
  assign REGSEL_ARF = and_49_out ? 3'b001 : 3'bz;  // Controlled_Buffer controlled_buffer_167
  assign FUNSEL_ARF = and_49_out ? 2'b01 : 2'bz;  // Controlled_Buffer controlled_buffer_168
  Subtractor #(.width(2)) subtractor_2 (.a(out_2[3:2]), .b(2'b01), .out(s2_01c));  // open: bin, bout
  Subtractor #(.width(2)) subtractor_3 (.a(out_2[6:5]), .b(2'b01), .out(s1_01c));  // open: bin, bout
  and and_51 (and_51_out, not_14_out, and_35_out);
  not not_16 (not_16_out, out_2[10]);
  and and_52 (and_52_out, and_51_out, not_16_out);
  assign OUTASEL = and_52_out ? out_2[3:2] : 2'bz;  // Controlled_Buffer controlled_buffer_169
  assign OUTBSEL = and_52_out ? out_2[6:5] : 2'bz;  // Controlled_Buffer controlled_buffer_170
  assign MUXCSEL = and_52_out ? 1'b1 : 1'bz;  // Controlled_Buffer controlled_buffer_171
  assign FUNSEL_ALU = and_52_out ? OPERATION : 4'bz;  // Controlled_Buffer controlled_buffer_172
  assign MUXASEL = and_52_out ? 2'b11 : 2'bz;  // Controlled_Buffer controlled_buffer_173
  assign REGSEL_RF = and_52_out ? {des_3bit[2:1], des_4bit} : 4'bz;  // Controlled_Buffer controlled_buffer_174
  assign FUNSEL_RF = and_52_out ? 2'b01 : 2'bz;  // Controlled_Buffer controlled_buffer_175
  and and_53 (and_53_out, and_51_out, out_2[10]);
  assign OUTASEL = and_53_out ? out_2[3:2] : 2'bz;  // Controlled_Buffer controlled_buffer_176
  assign OUTBSEL = and_53_out ? out_2[6:5] : 2'bz;  // Controlled_Buffer controlled_buffer_177
  assign MUXCSEL = and_53_out ? 1'b1 : 1'bz;  // Controlled_Buffer controlled_buffer_178
  assign FUNSEL_ALU = and_53_out ? OPERATION : 4'bz;  // Controlled_Buffer controlled_buffer_179
  assign MUXBSEL = and_53_out ? 2'b11 : 2'bz;  // Controlled_Buffer controlled_buffer_180
  assign REGSEL_ARF = and_53_out ? des_3bit : 3'bz;  // Controlled_Buffer controlled_buffer_181
  assign FUNSEL_ARF = and_53_out ? 2'b01 : 2'bz;  // Controlled_Buffer controlled_buffer_182

  // Other names for the same wires on the sheet: des_4bit[3:2] = des_3bit[2:1]; Address[7:0] = out_2[7:0];
  //   IR[15:0] = out_2; s2_01[1:0] = out_2[3:2]; SRCREG2[2:0] = out_2[4:2]; s2_3 = out_2[4]; s1_01[1:0] = out_2[6:5];
  //   SRCREG1[2:0] = out_2[7:5]; s1_3 = out_2[7]; AddressingMode = out_2[8]; des_01[1:0] = out_2[9:8];
  //   DESTREG[2:0] = out_2[10:8]; Regsel_t[1:0] = out_2[10:9]; des_0 = out_2[10]; OPCODE[4:0] = out_2[15:11];
  //   N_A_RF[3:2] = N_A_ARF[2:1]

  // Notes on the sheet:
  //   OPCODE D0
  //   D / IM
  //    D7 - D8 / T2
  //   ORGANIZATION
  //   DIRECT ADDRESS
  //   OPDCODE D1
  //   OPCODE  D2-D11-D12-D13 / T2 and D7-D8 / T3
  //   DECODE INSTRUCTION
  //   DECODE OPCODE
  //   OPDCODE D3
  //   OPDCODE D4
  //   SC RESET
  //   D7  D8 /  T4
  //   D11  D12  D13 /  T3
  //   D5-D6-D9-D10 /T3
  //   desreg = ARF
  //   D14 D15 D16
  //   D17
  //   D5-D6-D9-D10 / T2
  //   desreg = RF
  //   D18
endmodule
