// Logisim project project1.circ as structural Verilog: 11 circuits, main circuit flipflop
// inc
module increment (
  input  [7:0] INPUT,
  output [7:0] OUTPUT
);

  wire adder_1_cout, adder_2_cout, adder_3_cout, adder_4_cout, adder_5_cout, adder_6_cout, adder_7_cout;

  Adder #(.width(1)) adder_1 (.a(INPUT[0]), .b(1'b1), .out(OUTPUT[0]), .cin(1'b0), .cout(adder_1_cout));
  Adder #(.width(1)) adder_2 (.a(INPUT[1]), .b(1'b0), .out(OUTPUT[1]), .cin(adder_1_cout), .cout(adder_2_cout));
  Adder #(.width(1)) adder_3 (.a(INPUT[2]), .b(1'b0), .out(OUTPUT[2]), .cin(adder_2_cout), .cout(adder_3_cout));
  Adder #(.width(1)) adder_4 (.a(INPUT[3]), .b(1'b0), .out(OUTPUT[3]), .cin(adder_3_cout), .cout(adder_4_cout));
  Adder #(.width(1)) adder_5 (.a(INPUT[4]), .b(1'b0), .out(OUTPUT[4]), .cin(adder_4_cout), .cout(adder_5_cout));
  Adder #(.width(1)) adder_6 (.a(INPUT[5]), .b(1'b0), .out(OUTPUT[5]), .cin(adder_5_cout), .cout(adder_6_cout));
  Adder #(.width(1)) adder_7 (.a(INPUT[6]), .b(1'b0), .out(OUTPUT[6]), .cin(adder_6_cout), .cout(adder_7_cout));
  Adder #(.width(1)) adder_8 (.a(INPUT[7]), .b(1'b0), .out(OUTPUT[7]), .cin(adder_7_cout));  // open: cout
endmodule

// dec
module decrement (
  input  [7:0] INPUT,
  output [7:0] OUTPUT
);

  wire subtractor_1_bout, subtractor_2_bout, subtractor_3_bout, subtractor_4_bout, subtractor_5_bout,
       subtractor_6_bout, subtractor_7_bout;

  Subtractor #(.width(1)) subtractor_1 (.a(INPUT[0]), .b(1'b1), .out(OUTPUT[0]), .bin(1'b0), .bout(subtractor_1_bout));
  Subtractor #(.width(1)) subtractor_2 (
    .a(INPUT[1]), .b(1'b0), .out(OUTPUT[1]), .bin(subtractor_1_bout), .bout(subtractor_2_bout));
  Subtractor #(.width(1)) subtractor_3 (
    .a(INPUT[2]), .b(1'b0), .out(OUTPUT[2]), .bin(subtractor_2_bout), .bout(subtractor_3_bout));
  Subtractor #(.width(1)) subtractor_4 (
    .a(INPUT[3]), .b(1'b0), .out(OUTPUT[3]), .bin(subtractor_3_bout), .bout(subtractor_4_bout));
  Subtractor #(.width(1)) subtractor_5 (
    .a(INPUT[4]), .b(1'b0), .out(OUTPUT[4]), .bin(subtractor_4_bout), .bout(subtractor_5_bout));
  Subtractor #(.width(1)) subtractor_6 (
    .a(INPUT[5]), .b(1'b0), .out(OUTPUT[5]), .bin(subtractor_5_bout), .bout(subtractor_6_bout));
  Subtractor #(.width(1)) subtractor_7 (
    .a(INPUT[6]), .b(1'b0), .out(OUTPUT[6]), .bin(subtractor_6_bout), .bout(subtractor_7_bout));
  Subtractor #(.width(1)) subtractor_8 (
    .a(INPUT[7]), .b(1'b0), .out(OUTPUT[7]), .bin(subtractor_7_bout));  // open: bout
endmodule

// dff
module flipflop (
  input  CLK,
  input  [7:0] INPUT,
  input  EN,
  output [7:0] OUTPUT
);

  D_Flip_Flop d_ff_1 (.clk(CLK), .D(INPUT[0]), .Q(OUTPUT[0]), .en(EN));  // open: Qn, preset, reset
  D_Flip_Flop d_ff_2 (.clk(CLK), .D(INPUT[1]), .Q(OUTPUT[1]), .en(EN));  // open: Qn, preset, reset
  D_Flip_Flop d_ff_3 (.clk(CLK), .D(INPUT[2]), .Q(OUTPUT[2]), .en(EN));  // open: Qn, preset, reset
  D_Flip_Flop d_ff_4 (.clk(CLK), .D(INPUT[3]), .Q(OUTPUT[3]), .en(EN));  // open: Qn, preset, reset
  D_Flip_Flop d_ff_5 (.clk(CLK), .D(INPUT[4]), .Q(OUTPUT[4]), .en(EN));  // open: Qn, preset, reset
  D_Flip_Flop d_ff_6 (.clk(CLK), .D(INPUT[5]), .Q(OUTPUT[5]), .en(EN));  // open: Qn, preset, reset
  D_Flip_Flop d_ff_7 (.clk(CLK), .D(INPUT[6]), .Q(OUTPUT[6]), .en(EN));  // open: Qn, preset, reset
  D_Flip_Flop d_ff_8 (.clk(CLK), .D(INPUT[7]), .Q(OUTPUT[7]), .en(EN));  // open: Qn, preset, reset
endmodule

module inc16 (
  input  [15:0] INPUT,
  output [15:0] OUTPUT
);

  wire adder_1_cout, adder_2_cout, adder_3_cout, adder_4_cout, adder_5_cout, adder_6_cout, adder_7_cout,
       adder_8_cout, adder_9_cout, adder_10_cout, adder_11_cout, adder_12_cout, adder_13_cout, adder_14_cout,
       adder_15_cout;

  Adder #(.width(1)) adder_1 (.a(INPUT[0]), .b(1'b1), .out(OUTPUT[0]), .cin(1'b0), .cout(adder_1_cout));
  Adder #(.width(1)) adder_2 (.a(INPUT[1]), .b(1'b0), .out(OUTPUT[1]), .cin(adder_1_cout), .cout(adder_2_cout));
  Adder #(.width(1)) adder_3 (.a(INPUT[2]), .b(1'b0), .out(OUTPUT[2]), .cin(adder_2_cout), .cout(adder_3_cout));
  Adder #(.width(1)) adder_4 (.a(INPUT[3]), .b(1'b0), .out(OUTPUT[3]), .cin(adder_3_cout), .cout(adder_4_cout));
  Adder #(.width(1)) adder_5 (.a(INPUT[4]), .b(1'b0), .out(OUTPUT[4]), .cin(adder_4_cout), .cout(adder_5_cout));
  Adder #(.width(1)) adder_6 (.a(INPUT[5]), .b(1'b0), .out(OUTPUT[5]), .cin(adder_5_cout), .cout(adder_6_cout));
  Adder #(.width(1)) adder_7 (.a(INPUT[6]), .b(1'b0), .out(OUTPUT[6]), .cin(adder_6_cout), .cout(adder_7_cout));
  Adder #(.width(1)) adder_8 (.a(INPUT[7]), .b(1'b0), .out(OUTPUT[7]), .cin(adder_7_cout), .cout(adder_8_cout));
  Adder #(.width(1)) adder_9 (.a(INPUT[8]), .b(1'b0), .out(OUTPUT[8]), .cin(adder_8_cout), .cout(adder_9_cout));
  Adder #(.width(1)) adder_10 (.a(INPUT[9]), .b(1'b0), .out(OUTPUT[9]), .cin(adder_9_cout), .cout(adder_10_cout));
  Adder #(.width(1)) adder_11 (.a(INPUT[10]), .b(1'b0), .out(OUTPUT[10]), .cin(adder_10_cout), .cout(adder_11_cout));
  Adder #(.width(1)) adder_12 (.a(INPUT[11]), .b(1'b0), .out(OUTPUT[11]), .cin(adder_11_cout), .cout(adder_12_cout));
  Adder #(.width(1)) adder_13 (.a(INPUT[12]), .b(1'b0), .out(OUTPUT[12]), .cin(adder_12_cout), .cout(adder_13_cout));
  Adder #(.width(1)) adder_14 (.a(INPUT[13]), .b(1'b0), .out(OUTPUT[13]), .cin(adder_13_cout), .cout(adder_14_cout));
  Adder #(.width(1)) adder_15 (.a(INPUT[14]), .b(1'b0), .out(OUTPUT[14]), .cin(adder_14_cout), .cout(adder_15_cout));
  Adder #(.width(1)) adder_16 (.a(INPUT[15]), .b(1'b0), .out(OUTPUT[15]), .cin(adder_15_cout));  // open: cout
endmodule

module dec16 (
  input  [15:0] INPUT,
  output [15:0] OUTPUT
);

  wire subtractor_1_bout, subtractor_2_bout, subtractor_3_bout, subtractor_4_bout, subtractor_5_bout,
       subtractor_6_bout, subtractor_7_bout, subtractor_8_bout, subtractor_9_bout, subtractor_10_bout,
       subtractor_11_bout, subtractor_12_bout, subtractor_13_bout, subtractor_14_bout, subtractor_15_bout;

  Subtractor #(.width(1)) subtractor_1 (.a(INPUT[0]), .b(1'b1), .out(OUTPUT[0]), .bin(1'b0), .bout(subtractor_1_bout));
  Subtractor #(.width(1)) subtractor_2 (
    .a(INPUT[1]), .b(1'b0), .out(OUTPUT[1]), .bin(subtractor_1_bout), .bout(subtractor_2_bout));
  Subtractor #(.width(1)) subtractor_3 (
    .a(INPUT[2]), .b(1'b0), .out(OUTPUT[2]), .bin(subtractor_2_bout), .bout(subtractor_3_bout));
  Subtractor #(.width(1)) subtractor_4 (
    .a(INPUT[3]), .b(1'b0), .out(OUTPUT[3]), .bin(subtractor_3_bout), .bout(subtractor_4_bout));
  Subtractor #(.width(1)) subtractor_5 (
    .a(INPUT[4]), .b(1'b0), .out(OUTPUT[4]), .bin(subtractor_4_bout), .bout(subtractor_5_bout));
  Subtractor #(.width(1)) subtractor_6 (
    .a(INPUT[5]), .b(1'b0), .out(OUTPUT[5]), .bin(subtractor_5_bout), .bout(subtractor_6_bout));
  Subtractor #(.width(1)) subtractor_7 (
    .a(INPUT[6]), .b(1'b0), .out(OUTPUT[6]), .bin(subtractor_6_bout), .bout(subtractor_7_bout));
  Subtractor #(.width(1)) subtractor_8 (
    .a(INPUT[7]), .b(1'b0), .out(OUTPUT[7]), .bin(subtractor_7_bout), .bout(subtractor_8_bout));
  Subtractor #(.width(1)) subtractor_9 (
    .a(INPUT[8]), .b(1'b0), .out(OUTPUT[8]), .bin(subtractor_8_bout), .bout(subtractor_9_bout));
  Subtractor #(.width(1)) subtractor_10 (
    .a(INPUT[9]), .b(1'b0), .out(OUTPUT[9]), .bin(subtractor_9_bout), .bout(subtractor_10_bout));
  Subtractor #(.width(1)) subtractor_11 (
    .a(INPUT[10]), .b(1'b0), .out(OUTPUT[10]), .bin(subtractor_10_bout), .bout(subtractor_11_bout));
  Subtractor #(.width(1)) subtractor_12 (
    .a(INPUT[11]), .b(1'b0), .out(OUTPUT[11]), .bin(subtractor_11_bout), .bout(subtractor_12_bout));
  Subtractor #(.width(1)) subtractor_13 (
    .a(INPUT[12]), .b(1'b0), .out(OUTPUT[12]), .bin(subtractor_12_bout), .bout(subtractor_13_bout));
  Subtractor #(.width(1)) subtractor_14 (
    .a(INPUT[13]), .b(1'b0), .out(OUTPUT[13]), .bin(subtractor_13_bout), .bout(subtractor_14_bout));
  Subtractor #(.width(1)) subtractor_15 (
    .a(INPUT[14]), .b(1'b0), .out(OUTPUT[14]), .bin(subtractor_14_bout), .bout(subtractor_15_bout));
  Subtractor #(.width(1)) subtractor_16 (
    .a(INPUT[15]), .b(1'b0), .out(OUTPUT[15]), .bin(subtractor_15_bout));  // open: bout
endmodule

module dff16 (
  input  CLK,
  input  [15:0] INPUT,
  input  E,
  output [15:0] OUTPUT
);

  wire d_ff_8_qn;

  D_Flip_Flop d_ff_1 (.clk(CLK), .D(INPUT[0]), .Q(OUTPUT[0]), .en(E));  // open: Qn, preset, reset
  D_Flip_Flop d_ff_2 (.clk(CLK), .D(INPUT[1]), .Q(OUTPUT[1]), .en(E));  // open: Qn, preset, reset
  D_Flip_Flop d_ff_3 (.clk(CLK), .D(INPUT[2]), .Q(OUTPUT[2]), .en(E));  // open: Qn, preset, reset
  D_Flip_Flop d_ff_4 (.clk(CLK), .D(INPUT[3]), .Q(OUTPUT[3]), .en(E));  // open: Qn, preset, reset
  D_Flip_Flop d_ff_5 (.clk(CLK), .D(INPUT[4]), .Q(OUTPUT[4]), .en(E));  // open: Qn, preset, reset
  D_Flip_Flop d_ff_6 (.clk(CLK), .D(INPUT[5]), .Q(OUTPUT[5]), .en(E));  // open: Qn, preset, reset
  D_Flip_Flop d_ff_7 (.clk(CLK), .D(INPUT[6]), .Q(OUTPUT[6]), .en(E));  // open: Qn, preset, reset
  D_Flip_Flop d_ff_8 (.clk(CLK), .D(INPUT[7]), .Q(OUTPUT[7]), .Qn(d_ff_8_qn), .en(E));  // open: preset, reset
  D_Flip_Flop d_ff_9 (.clk(CLK), .D(INPUT[8]), .Q(OUTPUT[8]), .en(E));  // open: Qn, preset, reset
  D_Flip_Flop d_ff_10 (.clk(CLK), .D(INPUT[9]), .Q(OUTPUT[9]), .en(E));  // open: Qn, preset, reset
  D_Flip_Flop d_ff_11 (.clk(CLK), .D(INPUT[10]), .Q(OUTPUT[10]), .en(E));  // open: Qn, preset, reset
  D_Flip_Flop d_ff_12 (.clk(CLK), .D(INPUT[11]), .Q(OUTPUT[11]), .en(E));  // open: Qn, preset, reset
  D_Flip_Flop d_ff_13 (.clk(CLK), .D(INPUT[12]), .Q(OUTPUT[12]), .en(E));  // open: Qn, preset, reset
  D_Flip_Flop d_ff_14 (.clk(CLK), .D(INPUT[13]), .Q(OUTPUT[13]), .en(E));  // open: Qn, preset, reset
  D_Flip_Flop d_ff_15 (.clk(CLK), .D(INPUT[14]), .Q(OUTPUT[14]), .en(E));  // open: Qn, preset, reset
  D_Flip_Flop d_ff_16 (.clk(CLK), .D(INPUT[15]), .Q(OUTPUT[15]), .en(E));  // open: Qn, preset, reset
endmodule

module _8bitRegister (
  input  CLK,
  input  [7:0] I,
  input  [1:0] FunSel,
  input  E,
  output [7:0] Q
);

  wire [7:0] decrement_1_output, increment_1_output, multiplexer_1_out;

  Hex_Digit_Display hex_digit_display_1 (.value(I[7:4]));  // open: dp
  Hex_Digit_Display hex_digit_display_2 (.value(I[3:0]));  // open: dp
  Multiplexer #(.select(2), .width(8)) multiplexer_1 (
    .in0({8{1'b0}}), .in1(I), .in2(increment_1_output), .in3(decrement_1_output), .out(multiplexer_1_out),
    .sel(FunSel), .en(E));
  Hex_Digit_Display hex_digit_display_3 (.value(Q[7:4]));  // open: dp
  flipflop flipflop_1 (.CLK(CLK), .INPUT(multiplexer_1_out), .EN(E), .OUTPUT(Q));
  increment increment_1 (.INPUT(Q), .OUTPUT(increment_1_output));
  decrement decrement_1 (.INPUT(Q), .OUTPUT(decrement_1_output));
  Hex_Digit_Display hex_digit_display_4 (.value(Q[3:0]));  // open: dp
endmodule

module _16bitRegister (
  input  CLK,
  input  [15:0] I,
  input  [1:0] FunSel,
  input  E,
  output [15:0] Q
);

  wire [15:0] dec16_1_output, inc16_1_output, multiplexer_1_out;

  Hex_Digit_Display hex_digit_display_1 (.value(I[15:12]));  // open: dp
  Hex_Digit_Display hex_digit_display_2 (.value(I[11:8]));  // open: dp
  Hex_Digit_Display hex_digit_display_3 (.value(I[7:4]));  // open: dp
  Hex_Digit_Display hex_digit_display_4 (.value(I[3:0]));  // open: dp
  Multiplexer #(.select(2), .width(16)) multiplexer_1 (
    .in0({16{1'b0}}), .in1(I), .in2(inc16_1_output), .in3(dec16_1_output), .out(multiplexer_1_out),
    .sel(FunSel), .en(E));
  dff16 dff16_1 (.CLK(CLK), .INPUT(multiplexer_1_out), .E(E), .OUTPUT(Q));
  inc16 inc16_1 (.INPUT(Q), .OUTPUT(inc16_1_output));
  dec16 dec16_1 (.INPUT(Q), .OUTPUT(dec16_1_output));
  Hex_Digit_Display hex_digit_display_5 (.value(Q[11:8]));  // open: dp
  Hex_Digit_Display hex_digit_display_6 (.value(Q[15:12]));  // open: dp
  Hex_Digit_Display hex_digit_display_7 (.value(Q[7:4]));  // open: dp
  Hex_Digit_Display hex_digit_display_8 (.value(Q[3:0]));  // open: dp
endmodule

module RegisterFile (
  input  [3:0] RegSel,
  input  CLK,
  input  [7:0] I,
  input  [1:0] FunSel,
  input  [1:0] OutASel,
  input  [1:0] OutBSel,
  output [7:0] OutA,
  output [7:0] OutB
);

  wire [7:0] R0_q, R1_q, R2_q, R3_q;

  Hex_Digit_Display hex_digit_display_1 (.value(I[7:4]));  // open: dp
  Hex_Digit_Display hex_digit_display_2 (.value(I[3:0]));  // open: dp
  _8bitRegister R0 (.CLK(CLK), .I(I), .FunSel(FunSel), .E(RegSel[0]), .Q(R0_q));
  _8bitRegister R1 (.CLK(CLK), .I(I), .FunSel(FunSel), .E(RegSel[1]), .Q(R1_q));
  _8bitRegister R2 (.CLK(CLK), .I(I), .FunSel(FunSel), .E(RegSel[2]), .Q(R2_q));
  _8bitRegister R3 (.CLK(CLK), .I(I), .FunSel(FunSel), .E(RegSel[3]), .Q(R3_q));
  Multiplexer #(.select(2), .width(8), .enable("false")) multiplexer_1 (
    .in0(R0_q), .in1(R1_q), .in2(R2_q), .in3(R3_q), .out(OutA), .sel(OutASel));
  Multiplexer #(.select(2), .width(8), .enable("false")) multiplexer_2 (
    .in0(R0_q), .in1(R1_q), .in2(R2_q), .in3(R3_q), .out(OutB), .sel(OutBSel));
  Hex_Digit_Display hex_digit_display_3 (.value(OutA[7:4]));  // open: dp
  Hex_Digit_Display hex_digit_display_4 (.value(OutB[7:4]));  // open: dp
  Hex_Digit_Display hex_digit_display_5 (.value(OutA[3:0]));  // open: dp
  Hex_Digit_Display hex_digit_display_6 (.value(OutB[3:0]));  // open: dp
endmodule

module AddresRegFile (
  input  [2:0] RegSel,
  input  CLK,
  input  [7:0] I,
  input  [1:0] FunSel,
  input  [1:0] OutCSel,
  input  [1:0] OutDSel,
  output [7:0] OutC,
  output [7:0] OutD
);

  wire [7:0] AR_q, PC_q, SP_q;

  Hex_Digit_Display hex_digit_display_1 (.value(I[3:0]));  // open: dp
  Hex_Digit_Display hex_digit_display_2 (.value(I[7:4]));  // open: dp
  _8bitRegister PC (.CLK(CLK), .I(I), .FunSel(FunSel), .E(RegSel[0]), .Q(PC_q));
  _8bitRegister AR (.CLK(CLK), .I(I), .FunSel(FunSel), .E(RegSel[1]), .Q(AR_q));
  _8bitRegister SP (.CLK(CLK), .I(I), .FunSel(FunSel), .E(RegSel[2]), .Q(SP_q));
  Multiplexer #(.select(2), .width(8), .enable("false")) multiplexer_1 (
    .in0(PC_q), .in1(AR_q), .in2(SP_q), .in3(PC_q), .out(OutC), .sel(OutCSel));
  Multiplexer #(.select(2), .width(8), .enable("false")) multiplexer_2 (
    .in0(PC_q), .in1(AR_q), .in2(SP_q), .in3(PC_q), .out(OutD), .sel(OutDSel));
  Hex_Digit_Display hex_digit_display_3 (.value(OutC[7:4]));  // open: dp
  Hex_Digit_Display hex_digit_display_4 (.value(OutC[3:0]));  // open: dp
  Hex_Digit_Display hex_digit_display_5 (.value(OutD[3:0]));  // open: dp
  Hex_Digit_Display hex_digit_display_6 (.value(OutD[7:4]));  // open: dp
endmodule

module _16bitIR (
  input  CLK,
  input  [1:0] FunSel,
  input  L_H,
  input  [7:0] I,
  input  E,
  output [7:0] IR_0_7,
  output [7:0] IR_8_15
);

  wire [15:0] dec16_1_output, inc16_1_output, multiplexer_1_out;

  Hex_Digit_Display hex_digit_display_1 (.value(I[3:0]));  // open: dp
  Hex_Digit_Display hex_digit_display_2 (.value(I[7:4]));  // open: dp
  inc16 inc16_1 (.INPUT({IR_8_15, IR_0_7}), .OUTPUT(inc16_1_output));
  dec16 dec16_1 (.INPUT({IR_8_15, IR_0_7}), .OUTPUT(dec16_1_output));
  Multiplexer #(.select(3), .width(16)) multiplexer_1 (
    .in0({16{1'b0}}), .in1({16{1'b0}}), .in2(inc16_1_output), .in3(inc16_1_output), .in4(dec16_1_output),
    .in5(dec16_1_output), .in6({IR_8_15, I}), .in7({I, IR_0_7}), .out(multiplexer_1_out),
    .sel({FunSel, L_H}), .en(E));
  dff16 dff16_1 (.CLK(CLK), .INPUT(multiplexer_1_out), .E(E), .OUTPUT({IR_8_15, IR_0_7}));
endmodule
