// Logisim project project2-1.circ as structural Verilog: 15 circuits, main circuit main
module _4bit_D_flip_flop (
  input  [3:0] In,
  input  CLK,
  output [3:0] out_3
);

  D_Flip_Flop d_ff_1 (.clk(CLK), .D(In[0]), .Q(out_3[0]));  // open: Qn, preset, en, reset
  D_Flip_Flop d_ff_2 (.clk(CLK), .D(In[1]), .Q(out_3[1]));  // open: Qn, preset, en, reset
  D_Flip_Flop d_ff_3 (.clk(CLK), .D(In[2]), .Q(out_3[2]));  // open: Qn, preset, en, reset
  D_Flip_Flop d_ff_4 (.clk(CLK), .D(In[3]), .Q(out_3[3]));  // open: Qn, preset, en, reset
endmodule

module overflow (
  input  [7:0] A_B_or_A___B,
  input  [7:0] A,
  input  [7:0] B,
  input  [3:0] FUNSEL,
  input  EN,
  output O
);

  wire and_1_out, and_2_out, xnor_1_out, xnor_2_out, xor_1_out, xor_2_out;

  xor xor_1 (xor_1_out, A_B_or_A___B[7], A[7]);
  xnor xnor_1 (xnor_1_out, A[7], B[7]);
  xnor xnor_2 (xnor_2_out, B[7], A_B_or_A___B[7]);
  xor xor_2 (xor_2_out, A_B_or_A___B[7], B[7]);
  and and_1 (and_1_out, xnor_2_out, xor_2_out);
  and and_2 (and_2_out, xor_1_out, xnor_1_out);
  Multiplexer #(.select(2)) multiplexer_1 (
    .in0(and_2_out), .in1(and_2_out), .in2(and_1_out), .out(O), .sel(FUNSEL[1:0]), .en(EN));  // open: in3
endmodule

module carry (
  input  [3:0] FUNSEL,
  input  in_2
);

  wire and_1_out, nand_1_out, not_1_out;

  nand nand_1 (nand_1_out, FUNSEL[0], FUNSEL[1]);
  not not_1 (not_1_out, FUNSEL[3]);
  and and_1 (and_1_out, nand_1_out, FUNSEL[2], not_1_out);
endmodule

module LSL (
  input  [7:0] In,
  input  Cin,
  output [7:0] out_3,
  output [1:0] C___O
);

  Shifter shifter_1 (.in(In), .\dist (3'b001), .out(out_3));

  assign C___O[1] = In[7];
endmodule

module LSR (
  input  [7:0] in_1,
  input  Cin,
  output [7:0] out_3,
  output [1:0] C___O
);

  Shifter #(.shift("lr")) shifter_1 (.in(in_1), .\dist (3'b001), .out(out_3));

  assign C___O[1] = in_1[0];
endmodule

module CSL (
  input  [7:0] IN,
  input  Cin,
  output [7:0] out_3,
  output [1:0] C___O
);

  xor xor_1 (C___O[0], IN[6], IN[7]);

  assign C___O[1] = IN[7];
  assign out_3 = {IN[6:0], Cin};
endmodule

module CSR (
  input  [7:0] IN,
  input  Cin,
  output [7:0] out_3,
  output [1:0] C___O
);

  xor xor_1 (C___O[0], IN[7], Cin);

  assign C___O[1] = IN[0];
  assign out_3 = {Cin, IN[7:1]};
endmodule

// Arithmetic
module Arithmetic_Unit (
  input  Cin,
  input  [3:0] FUNSEL,
  input  EN,
  input  [7:0] A,
  input  [7:0] B,
  output [7:0] OutArithmetic,
  output [1:0] C___O
);

  wire adder_1_cout, adder_2_cout, adder_3_cout;
  wire [7:0] adder_1_out, adder_2_out, adder_3_out, not_1_out;

  assign not_1_out = ~B;  // NOT_Gate not_1, 8 bits wide
  Adder adder_1 (.a(A), .b(not_1_out), .out(adder_1_out), .cin(1'b1), .cout(adder_1_cout));
  Adder adder_2 (.a(A), .b(B), .out(adder_2_out), .cout(adder_2_cout));  // open: cin
  Adder adder_3 (.a(A), .b(B), .out(adder_3_out), .cin(Cin), .cout(adder_3_cout));
  Multiplexer #(.select(2), .width(8)) multiplexer_1 (
    .in0(adder_2_out), .in1(adder_3_out), .in2(adder_1_out), .out(OutArithmetic), .sel(FUNSEL[1:0]), .en(EN));  // open: in3
  Multiplexer #(.select(2)) multiplexer_2 (
    .in0(adder_2_cout), .in1(adder_3_cout), .in2(adder_1_cout), .out(C___O[1]), .sel(FUNSEL[1:0]), .en(EN));  // open: in3
  overflow overflow_1 (.A_B_or_A___B(OutArithmetic), .A(A), .B(B), .FUNSEL(FUNSEL), .EN(EN), .O(C___O[0]));
endmodule

module ZERO (
  input  [7:0] IN,
  output Out
);

  nor nor_1 (Out, IN[0], IN[1], IN[2], IN[3], IN[4], IN[5], IN[6], IN[7]);
endmodule

// shift
module Shift_Unit (
  input  [7:0] A,
  input  Cin,
  input  [3:0] FUNSEL,
  input  in_4,
  output [7:0] \OUTSHİFT ,
  output [1:0] C___O
);

  wire [1:0] asl_1_c___o, asr_1_c___o, csl_1_c___o, csr_1_c___o, lsl_1_c___o, lsr_1_c___o;
  wire [7:0] asl_1_out_3, asr_1_out_3, csl_1_out_3, csr_1_out_3, lsl_1_out_3, lsr_1_out_3;

  ASL asl_1 (.IN(A), .Cin(Cin), .out_3(asl_1_out_3), .C___O(asl_1_c___o));
  ASR asr_1 (.IN(A), .Cin(Cin), .out_3(asr_1_out_3), .C___O(asr_1_c___o));
  CSL csl_1 (.IN(A), .Cin(Cin), .out_3(csl_1_out_3), .C___O(csl_1_c___o));
  CSR csr_1 (.IN(A), .Cin(Cin), .out_3(csr_1_out_3), .C___O(csr_1_c___o));
  LSL lsl_1 (.In(A), .out_3(lsl_1_out_3), .C___O(lsl_1_c___o), .Cin(Cin));
  LSR lsr_1 (.in_1(A), .Cin(Cin), .out_3(lsr_1_out_3), .C___O(lsr_1_c___o));
  Multiplexer #(.select(3), .width(2)) multiplexer_1 (
    .in2(lsl_1_c___o), .in3(lsr_1_c___o), .in4(asl_1_c___o), .in5(asr_1_c___o), .in6(csl_1_c___o),
    .in7(csr_1_c___o), .out(C___O), .sel(FUNSEL[2:0]), .en(in_4));  // open: in0, in1
  Multiplexer #(.select(3), .width(8)) multiplexer_2 (
    .in2(lsl_1_out_3), .in3(lsr_1_out_3), .in4(asl_1_out_3), .in5(asr_1_out_3), .in6(csl_1_out_3),
    .in7(csr_1_out_3), .out(\OUTSHİFT ), .sel(FUNSEL[2:0]), .en(in_4));  // open: in0, in1
endmodule

module ASL (
  input  [7:0] IN,
  input  Cin,
  output [7:0] out_3,
  output [1:0] C___O
);

  xor xor_1 (C___O[0], IN[6], IN[7]);
  not not_1 (out_3[0], 1'b1);

  assign out_3[7:1] = IN[6:0];
endmodule

module ASR (
  input  [7:0] IN,
  input  Cin,
  output [7:0] out_3,
  output [1:0] C___O
);

  not not_1 (C___O[0], 1'b1);

  assign out_3 = {{2{IN[7]}}, IN[6:1]};
endmodule

module C_Selection (
  input  [3:0] In,
  output [1:0] CarrySelect
);

  wire and_1_out, and_2_out, not_1_out, not_2_out, not_3_out;

  not not_1 (not_1_out, In[3]);
  not not_2 (not_2_out, In[1]);
  not not_3 (not_3_out, In[0]);
  and and_1 (and_1_out, not_2_out, In[2], not_1_out);
  and and_2 (and_2_out, not_3_out, In[2], not_1_out);
  or or_1 (CarrySelect[0], and_1_out, and_2_out);
  and and_3 (CarrySelect[1], In[1], In[3]);
endmodule

module OverflowSelection (
  input  [3:0] in_1,
  output [1:0] CarrySelect
);

  wire and_1_out, and_2_out, and_3_out, and_4_out, not_1_out, not_2_out, not_3_out;

  not not_1 (not_1_out, in_1[3]);
  not not_2 (not_2_out, in_1[1]);
  not not_3 (not_3_out, in_1[0]);
  and and_1 (and_1_out, not_1_out, in_1[2], not_2_out);
  and and_2 (and_2_out, not_3_out, in_1[2], not_1_out);
  and and_3 (and_3_out, not_3_out, in_1[2], in_1[3]);
  and and_4 (and_4_out, in_1[1], in_1[2], in_1[3]);
  or or_1 (CarrySelect[0], and_1_out, and_2_out);
  or or_2 (CarrySelect[1], and_3_out, and_4_out);
endmodule

// ALU
module main (
  input  [7:0] A,
  input  CLK,
  input  [7:0] B,
  input  Cin,
  input  EN,
  input  [3:0] FUNSEL,
  output [7:0] OUTALU,
  output [3:0] Z_C_N_O
);

  wire or_1_out;
  wire [1:0] arithmetic_unit_1_c___o, C_Selection_carryselect, OverflowSelection_carryselect,
       shift_unit_1_c___o;
  wire [3:0] multiplexer_2_out;
  wire [7:0] and_1_out, arithmetic_unit_1_outarithmetic, not_1_out, not_2_out, or_2_out,
       \shift_unit_1_outshi̇ft , xor_1_out;

  or or_1 (or_1_out, Cin, Z_C_N_O[2]);
  assign not_1_out = ~A;  // NOT_Gate not_1, 8 bits wide
  assign not_2_out = ~B;  // NOT_Gate not_2, 8 bits wide
  Arithmetic_Unit arithmetic_unit_1 (
    .Cin(or_1_out), .A(A), .B(B), .OutArithmetic(arithmetic_unit_1_outarithmetic),
    .C___O(arithmetic_unit_1_c___o), .FUNSEL(FUNSEL), .EN(EN));
  Shift_Unit shift_unit_1 (
    .A(A), .Cin(Z_C_N_O[2]), .FUNSEL(FUNSEL), .\OUTSHİFT (\shift_unit_1_outshi̇ft ),
    .C___O(shift_unit_1_c___o), .in_4(EN));
  C_Selection C_Selection (.In(FUNSEL), .CarrySelect(C_Selection_carryselect));
  OverflowSelection OverflowSelection (.in_1(FUNSEL), .CarrySelect(OverflowSelection_carryselect));
  assign and_1_out = A & B;  // AND_Gate and_1, 8 bits wide
  assign or_2_out = A | B;  // OR_Gate or_2, 8 bits wide
  Multiplexer #(.select(2)) multiplexer_1 (
    .in0(Z_C_N_O[2]), .in1(arithmetic_unit_1_c___o[1]), .in2(shift_unit_1_c___o[1]),
    .out(multiplexer_2_out[2]), .sel(C_Selection_carryselect), .en(EN));  // open: in3
  Multiplexer #(.select(2)) multiplexer_2 (
    .in0(Z_C_N_O[0]), .in1(arithmetic_unit_1_c___o[0]), .in2(shift_unit_1_c___o[0]),
    .out(multiplexer_2_out[0]), .sel(OverflowSelection_carryselect), .en(EN));  // open: in3
  assign xor_1_out = A ^ B;  // XOR_Gate xor_1, 8 bits wide
  Multiplexer #(.select(4), .width(8)) multiplexer_3 (
    .in0(A), .in1(B), .in2(not_1_out), .in3(not_2_out), .in4(arithmetic_unit_1_outarithmetic),
    .in5(arithmetic_unit_1_outarithmetic), .in6(arithmetic_unit_1_outarithmetic), .in7(and_1_out),
    .in8(or_2_out), .in9(xor_1_out), .in10(\shift_unit_1_outshi̇ft ), .in11(\shift_unit_1_outshi̇ft ),
    .in12(\shift_unit_1_outshi̇ft ), .in13(\shift_unit_1_outshi̇ft ), .in14(\shift_unit_1_outshi̇ft ),
    .in15(\shift_unit_1_outshi̇ft ), .out(OUTALU), .sel(FUNSEL), .en(EN));
  ZERO ZERO_CHECK (.IN(OUTALU), .Out(multiplexer_2_out[3]));
  _4bit_D_flip_flop _4_bit_D (
    .In({multiplexer_2_out[3:2], OUTALU[7], multiplexer_2_out[0]}), .out_3(Z_C_N_O), .CLK(CLK));
endmodule
