// Logisim project project2-2.circ as structural Verilog: 1 circuit, main circuit main
// Organization
module main (
  input  EN,
  input  MuxCSel,
  input  [3:0] FunSel,
  input  [1:0] OutASel,
  input  [1:0] OutBSel,
  input  [1:0] FunSel_2,
  input  [3:0] RegSel,
  input  [1:0] MuxASel,
  input  [1:0] MuxBSel,
  input  [1:0] OutCSel,
  input  in_11,
  input  in_12,
  input  in_13,
  input  in_14,
  input  [1:0] OutDSel,
  input  [1:0] FunSel_3,
  input  [2:0] RegSel_2,
  input  L___H_prime,
  input  [1:0] FUNSEL_4,
  input  EN_IR,
  input  CLK,
  output [3:0] FlagRegister,
  output [7:0] IR__8_15,
  output [15:0] IR
);

  wire [7:0] addresregfile_1_outc, addresregfile_1_outd, main_1_outalu, multiplexer_1_out, multiplexer_2_out,
       multiplexer_3_out, ram_1_data, registerfile_1_outa, registerfile_1_outb;

  Multiplexer #(.select(2), .width(8)) multiplexer_1 (
    .in0(IR[7:0]), .in1(ram_1_data), .in2(addresregfile_1_outc), .in3(main_1_outalu),
    .out(multiplexer_1_out), .sel(MuxASel), .en(EN));
  _16bitIR u_16bitir_1 (
    .FunSel(FUNSEL_4), .L_H(L___H_prime), .I(ram_1_data), .E(EN_IR), .IR_0_7(IR[7:0]), .IR_8_15(IR[15:8]),
    .CLK(CLK));
  RegisterFile registerfile_1 (
    .RegSel(RegSel), .I(multiplexer_1_out), .FunSel(FunSel_2), .OutASel(OutASel), .OutBSel(OutBSel),
    .OutA(registerfile_1_outa), .OutB(registerfile_1_outb), .CLK(CLK));
  Multiplexer #(.select(2), .width(8)) multiplexer_2 (
    .in1(IR[7:0]), .in2(ram_1_data), .in3(main_1_outalu), .out(multiplexer_2_out), .sel(MuxBSel), .en(EN));  // open: in0
  Multiplexer #(.width(8)) multiplexer_3 (
    .in0(multiplexer_1_out), .in1(registerfile_1_outa), .out(multiplexer_3_out), .sel(MuxCSel), .en(EN));
  AddresRegFile addresregfile_1 (
    .RegSel(RegSel_2), .I(multiplexer_2_out), .FunSel(FunSel_3), .OutCSel(OutCSel), .OutDSel(OutDSel),
    .OutC(addresregfile_1_outc), .OutD(addresregfile_1_outd), .CLK(CLK));
  project2_1_main main_1 (
    .A(multiplexer_3_out), .B(registerfile_1_outb), .EN(EN), .FUNSEL(FunSel), .OUTALU(main_1_outalu),
    .Z_C_N_O(FlagRegister), .Cin(FlagRegister[2]), .CLK(CLK));
  RAM #(.bus("separate")) ram_1 (
    .addr(addresregfile_1_outd), .din(main_1_outalu), .data(ram_1_data), .str(in_11), .sel(in_12), .clk(CLK),
    .ld(in_13), .clr(in_14));

  assign IR__8_15 = IR[15:8];
endmodule
